// Logisim project CPU.circ as structural Verilog: 13 circuits, main circuit main
module main (
);

  wire CLK_out, core_1_dmwe, core_1_inputc, core_1_outputc, GLOBAL_RESET_out, keyboard_1_avail, not_1_out;
  wire [6:0] core_1_charout, keyboard_1_data;
  wire [15:0] core_1_dmwa, core_1_dmwd, core_1_pc, ram_1_data, rom_1_data;

  Keyboard #(.trigger("falling")) keyboard_1 (
    .clk(CLK_out), .re(core_1_inputc), .clr(GLOBAL_RESET_out), .avail(keyboard_1_avail),
    .data(keyboard_1_data));
  Clock CLK (.out(CLK_out));
  Button GLOBAL_RESET (.out(GLOBAL_RESET_out));
  ROM #(.addrWidth(16), .dataWidth(16)) rom_1 (.addr(core_1_pc), .data(rom_1_data));  // open: sel
  not not_1 (not_1_out, CLK_out);
  CORE core_1 (
    .CLK(CLK_out), .GLOBAL_RESET(GLOBAL_RESET_out), .DMro(ram_1_data), .CHARIN(keyboard_1_data),
    .VALCHAR(keyboard_1_avail), .INSTRUCTION(rom_1_data), .PC(core_1_pc), .DMWA(core_1_dmwa),
    .DMwd(core_1_dmwd), .CHAROUT(core_1_charout), .DMwe(core_1_dmwe), .INPUTC(core_1_inputc),
    .OUTPUTC(core_1_outputc));
  RAM #(.addrWidth(16), .dataWidth(16), .bus("separate")) ram_1 (
    .addr(core_1_dmwa), .din(core_1_dmwd), .data(ram_1_data), .str(core_1_dmwe), .clk(not_1_out));  // open: sel, ld, clr
  TTY #(.trigger("falling")) tty_1 (.data(core_1_charout), .clk(CLK_out), .we(core_1_outputc), .clr(GLOBAL_RESET_out));

  // Notes on the sheet:
  //   KEYBOARD
  //   INSTRUCTION ROM
  //   contents of rom_1 (hex, n*v repeats v):
  //   1048 520d 1244 520d 1251 5209 1241 d117 1048 520d 1242 520d 125f 5209 1241 d117 1048 520d 1243 520d
  //   1252 5209 1240 d117 1048 520d 1244 520d 1246 5209 1240 d117 1048 520d 1244 520d 124b 5209 1241 d117
  //   1048 520d 1244 520d 1258 5209 1240 d117 10c5 1104 1902 193f 970b 1048 520d 1240 520d 1254 5209 1241
  //   d117 903f 1fc1 903f 1048 520d 1240 520d 124d 5209 1241 d117 718 1905 970b 1048 520d 1240 520d 1246
  //   5209 1241 d117 903f 1fc1 903f 1048 520d 1240 520d 1240 5209 1240 d117 26e8 2720 994b 1048 520d 1241
  //   520d 1242 5209 1241 d117 903f 1fc1 903f 1048 520d 1240 520d 125c 5209 1240 d117 10c1 561e 111f 191f
  //   1902 970b 1048 520d 1242 520d 124b 5209 1240 d117 903f 1fc1 903f 1048 520d 1242 520d 1244 5209 1241
  //   d117 661e 16ff 960b 1048 520d 1242 520d 1258 5209 1241 d117 903f 1fc1 903f 1048 520d 1242 520d 1252
  //   5209 1240 d117 10c1 561f 16ff 1101 5826 1901 38e0 1141 5a2e 1b41 9b0b 1048 520d 1241 520d 1250 5209
  //   1240 d117 903f 1fc1 903f 1048 520d 1241 520d 1249 5209 1241 d117 10c1 561e 1118 4728 111f 191f 191a
  //   9b0b 1048 520d 1241 520d 125d 5209 1241 d117 903f 1fc1 903f 1048 520d 1241 520d 1257 5209 1240 d117
  //   10c5 561e 561e 1101 8701 7741 9b0b 1048 520d 1243 520d 124b 5209 1241 d117 903f 1fc1 903f 1048 520d
  //   1243 520d 1245 5209 1241 d117 10e9 1128 a8cb 1048 520d 1243 520d 125f 5209 1240 d117 903f 1fc1 903f
  //   1048 520d 1243 520d 1258 5209 1241 d117 1048 520d 1245 520d 1240 5209 1240 d117 903f 1fc1 903f 7280
  //   f400 1241 9081 b117 108a f400 c038
  //   DATA RAM
  //   PRO UNIX DISPLAY
endmodule

module _16_bit_Reg (
  input  [15:0] \input ,
  input  RESET,
  input  WE,
  input  CLK,
  output [15:0] \output 
);

  D_Flip_Flop #(.trigger("falling")) d_ff_1 (
    .clk(CLK), .D(\input [0]), .Q(\output [0]), .en(WE), .reset(RESET));  // open: Qn, preset
  D_Flip_Flop #(.trigger("falling")) d_ff_2 (
    .clk(CLK), .D(\input [1]), .Q(\output [1]), .en(WE), .reset(RESET));  // open: Qn, preset
  D_Flip_Flop #(.trigger("falling")) d_ff_3 (
    .clk(CLK), .D(\input [2]), .Q(\output [2]), .en(WE), .reset(RESET));  // open: Qn, preset
  D_Flip_Flop #(.trigger("falling")) d_ff_4 (
    .clk(CLK), .D(\input [3]), .Q(\output [3]), .en(WE), .reset(RESET));  // open: Qn, preset
  D_Flip_Flop #(.trigger("falling")) d_ff_5 (
    .clk(CLK), .D(\input [4]), .Q(\output [4]), .en(WE), .reset(RESET));  // open: Qn, preset
  D_Flip_Flop #(.trigger("falling")) d_ff_6 (
    .clk(CLK), .D(\input [5]), .Q(\output [5]), .en(WE), .reset(RESET));  // open: Qn, preset
  D_Flip_Flop #(.trigger("falling")) d_ff_7 (
    .clk(CLK), .D(\input [6]), .Q(\output [6]), .en(WE), .reset(RESET));  // open: Qn, preset
  D_Flip_Flop #(.trigger("falling")) d_ff_8 (
    .clk(CLK), .D(\input [7]), .Q(\output [7]), .en(WE), .reset(RESET));  // open: Qn, preset
  D_Flip_Flop #(.trigger("falling")) d_ff_9 (
    .clk(CLK), .D(\input [8]), .Q(\output [8]), .en(WE), .reset(RESET));  // open: Qn, preset
  D_Flip_Flop #(.trigger("falling")) d_ff_10 (
    .clk(CLK), .D(\input [9]), .Q(\output [9]), .en(WE), .reset(RESET));  // open: Qn, preset
  D_Flip_Flop #(.trigger("falling")) d_ff_11 (
    .clk(CLK), .D(\input [10]), .Q(\output [10]), .en(WE), .reset(RESET));  // open: Qn, preset
  D_Flip_Flop #(.trigger("falling")) d_ff_12 (
    .clk(CLK), .D(\input [11]), .Q(\output [11]), .en(WE), .reset(RESET));  // open: Qn, preset
  D_Flip_Flop #(.trigger("falling")) d_ff_13 (
    .clk(CLK), .D(\input [12]), .Q(\output [12]), .en(WE), .reset(RESET));  // open: Qn, preset
  D_Flip_Flop #(.trigger("falling")) d_ff_14 (
    .clk(CLK), .D(\input [13]), .Q(\output [13]), .en(WE), .reset(RESET));  // open: Qn, preset
  D_Flip_Flop #(.trigger("falling")) d_ff_15 (
    .clk(CLK), .D(\input [14]), .Q(\output [14]), .en(WE), .reset(RESET));  // open: Qn, preset
  D_Flip_Flop #(.trigger("falling")) d_ff_16 (
    .clk(CLK), .D(\input [15]), .Q(\output [15]), .en(WE), .reset(RESET));  // open: Qn, preset
endmodule

module RegFile (
  input  CLK,
  input  GLOBAL_RESET,
  input  [2:0] RS2,
  input  GLOBAL_REG_WE,
  input  [2:0] RD,
  input  [15:0] RDVAL,
  input  [2:0] RS1,
  output [15:0] RS2VAL,
  output [15:0] RS1VAL
);

  wire and_1_out, and_2_out, and_3_out, and_4_out, and_5_out, and_6_out, and_7_out, decoder_1_out1,
       decoder_1_out2, decoder_1_out3, decoder_1_out4, decoder_1_out5, decoder_1_out6, decoder_1_out7;
  wire [15:0] n16_bit_reg_1_output, n16_bit_reg_2_output, n16_bit_reg_3_output, n16_bit_reg_4_output,
       n16_bit_reg_5_output, n16_bit_reg_6_output, n16_bit_reg_7_output, n16_bit_reg_8_output;

  and and_1 (and_1_out, GLOBAL_REG_WE, decoder_1_out7);
  _16_bit_Reg u_16_bit_reg_1 (
    .\input (RDVAL), .RESET(GLOBAL_RESET), .WE(and_1_out), .CLK(CLK), .\output (n16_bit_reg_1_output));
  and and_2 (and_2_out, GLOBAL_REG_WE, decoder_1_out6);
  _16_bit_Reg u_16_bit_reg_2 (
    .\input (RDVAL), .RESET(GLOBAL_RESET), .WE(and_2_out), .CLK(CLK), .\output (n16_bit_reg_2_output));
  and and_3 (and_3_out, GLOBAL_REG_WE, decoder_1_out5);
  _16_bit_Reg u_16_bit_reg_3 (
    .\input (RDVAL), .RESET(GLOBAL_RESET), .WE(and_3_out), .CLK(CLK), .\output (n16_bit_reg_3_output));
  Decoder #(.select(3), .enable("false")) decoder_1 (
    .out1(decoder_1_out1), .out2(decoder_1_out2), .out3(decoder_1_out3), .out4(decoder_1_out4),
    .out5(decoder_1_out5), .out6(decoder_1_out6), .out7(decoder_1_out7), .sel(RD));  // open: out0
  and and_4 (and_4_out, GLOBAL_REG_WE, decoder_1_out4);
  _16_bit_Reg u_16_bit_reg_4 (
    .\input (RDVAL), .RESET(GLOBAL_RESET), .WE(and_4_out), .CLK(CLK), .\output (n16_bit_reg_4_output));
  and and_5 (and_5_out, GLOBAL_REG_WE, decoder_1_out3);
  _16_bit_Reg u_16_bit_reg_5 (
    .\input (RDVAL), .RESET(GLOBAL_RESET), .WE(and_5_out), .CLK(CLK), .\output (n16_bit_reg_5_output));
  and and_6 (and_6_out, GLOBAL_REG_WE, decoder_1_out2);
  _16_bit_Reg u_16_bit_reg_6 (
    .\input (RDVAL), .RESET(GLOBAL_RESET), .WE(and_6_out), .CLK(CLK), .\output (n16_bit_reg_6_output));
  and and_7 (and_7_out, GLOBAL_REG_WE, decoder_1_out1);
  _16_bit_Reg u_16_bit_reg_7 (
    .\input (RDVAL), .RESET(GLOBAL_RESET), .WE(and_7_out), .CLK(CLK), .\output (n16_bit_reg_7_output));
  _16_bit_Reg u_16_bit_reg_8 (
    .\input (RDVAL), .RESET(GLOBAL_RESET), .WE(1'b0), .CLK(CLK), .\output (n16_bit_reg_8_output));
  Multiplexer #(.select(3), .width(16), .enable("false")) multiplexer_1 (
    .in0(n16_bit_reg_8_output), .in1(n16_bit_reg_7_output), .in2(n16_bit_reg_6_output),
    .in3(n16_bit_reg_5_output), .in4(n16_bit_reg_4_output), .in5(n16_bit_reg_3_output),
    .in6(n16_bit_reg_2_output), .in7(n16_bit_reg_1_output), .out(RS2VAL), .sel(RS2));
  Multiplexer #(.select(3), .width(16), .enable("false")) multiplexer_2 (
    .in0(n16_bit_reg_8_output), .in1(n16_bit_reg_7_output), .in2(n16_bit_reg_6_output),
    .in3(n16_bit_reg_5_output), .in4(n16_bit_reg_4_output), .in5(n16_bit_reg_3_output),
    .in6(n16_bit_reg_2_output), .in7(n16_bit_reg_1_output), .out(RS1VAL), .sel(RS1));
endmodule

module Full_Adder (
  input  Cin,
  input  b,
  input  a,
  input  sub,
  output sum,
  output Cout
);

  wire and_1_out, and_2_out, xor_2_out, xor_3_out;

  or or_1 (Cout, and_1_out, and_2_out);
  and and_1 (and_1_out, xor_2_out, Cin);
  and and_2 (and_2_out, xor_3_out, b);
  xor xor_1 (sum, xor_2_out, Cin);
  xor xor_2 (xor_2_out, b, xor_3_out);
  xor xor_3 (xor_3_out, a, sub);
endmodule

module ALU_Slice (
  input  Cin,
  input  a,
  input  b,
  input  [1:0] Func,
  output Q,
  output Cout
);

  wire and_1_out, full_adder_1_sum, xor_1_out;

  Full_Adder full_adder_1 (.Cout(Cout), .Cin(Cin), .sum(full_adder_1_sum), .b(b), .a(a), .sub(Func[0]));
  and and_1 (and_1_out, b, a);
  xor xor_1 (xor_1_out, b, a);
  Multiplexer #(.select(2), .enable("false")) multiplexer_1 (
    .in0(full_adder_1_sum), .in1(full_adder_1_sum), .in2(and_1_out), .in3(xor_1_out), .out(Q), .sel(Func));
endmodule

module ALU (
  input  [1:0] ALUop,
  input  [15:0] InputData2,
  input  [15:0] InputData1,
  output Zero,
  output [15:0] OutputData,
  output OVERFLOW,
  output NEGATIVE
);

  wire alu_slice_1_cout, alu_slice_2_cout, alu_slice_3_cout, alu_slice_4_cout, alu_slice_5_cout,
       alu_slice_6_cout, alu_slice_7_cout, alu_slice_8_cout, alu_slice_9_cout, alu_slice_10_cout,
       alu_slice_11_cout, alu_slice_12_cout, alu_slice_13_cout, alu_slice_14_cout, alu_slice_15_cout,
       alu_slice_16_cout, or_1_out;

  xor xor_1 (OVERFLOW, alu_slice_1_cout, alu_slice_2_cout);
  ALU_Slice alu_slice_1 (
    .a(InputData1[15]), .b(InputData2[15]), .Q(NEGATIVE), .Cin(alu_slice_2_cout), .Cout(alu_slice_1_cout),
    .Func(ALUop));
  ALU_Slice alu_slice_2 (
    .a(InputData1[14]), .b(InputData2[14]), .Q(OutputData[14]), .Cin(alu_slice_3_cout),
    .Cout(alu_slice_2_cout), .Func(ALUop));
  ALU_Slice alu_slice_3 (
    .a(InputData1[13]), .b(InputData2[13]), .Q(OutputData[13]), .Cin(alu_slice_4_cout),
    .Cout(alu_slice_3_cout), .Func(ALUop));
  ALU_Slice alu_slice_4 (
    .a(InputData1[12]), .b(InputData2[12]), .Q(OutputData[12]), .Cin(alu_slice_5_cout),
    .Cout(alu_slice_4_cout), .Func(ALUop));
  ALU_Slice alu_slice_5 (
    .a(InputData1[11]), .b(InputData2[11]), .Q(OutputData[11]), .Cin(alu_slice_6_cout),
    .Cout(alu_slice_5_cout), .Func(ALUop));
  ALU_Slice alu_slice_6 (
    .a(InputData1[10]), .b(InputData2[10]), .Q(OutputData[10]), .Cin(alu_slice_7_cout),
    .Cout(alu_slice_6_cout), .Func(ALUop));
  ALU_Slice alu_slice_7 (
    .a(InputData1[9]), .b(InputData2[9]), .Q(OutputData[9]), .Cin(alu_slice_8_cout), .Cout(alu_slice_7_cout),
    .Func(ALUop));
  or or_1 (or_1_out, OutputData[0], OutputData[1], OutputData[2], OutputData[3], OutputData[4], OutputData[5], OutputData[6], OutputData[7], OutputData[8], OutputData[9], OutputData[10], OutputData[11], OutputData[12], OutputData[13], OutputData[14], NEGATIVE);
  ALU_Slice alu_slice_8 (
    .a(InputData1[8]), .b(InputData2[8]), .Q(OutputData[8]), .Cin(alu_slice_9_cout), .Cout(alu_slice_8_cout),
    .Func(ALUop));
  not not_1 (Zero, or_1_out);
  ALU_Slice alu_slice_9 (
    .a(InputData1[7]), .b(InputData2[7]), .Q(OutputData[7]), .Cin(alu_slice_10_cout),
    .Cout(alu_slice_9_cout), .Func(ALUop));
  ALU_Slice alu_slice_10 (
    .a(InputData1[6]), .b(InputData2[6]), .Q(OutputData[6]), .Cin(alu_slice_11_cout),
    .Cout(alu_slice_10_cout), .Func(ALUop));
  ALU_Slice alu_slice_11 (
    .a(InputData1[5]), .b(InputData2[5]), .Q(OutputData[5]), .Cin(alu_slice_12_cout),
    .Cout(alu_slice_11_cout), .Func(ALUop));
  ALU_Slice alu_slice_12 (
    .a(InputData1[4]), .b(InputData2[4]), .Q(OutputData[4]), .Cin(alu_slice_13_cout),
    .Cout(alu_slice_12_cout), .Func(ALUop));
  ALU_Slice alu_slice_13 (
    .a(InputData1[3]), .b(InputData2[3]), .Q(OutputData[3]), .Cin(alu_slice_14_cout),
    .Cout(alu_slice_13_cout), .Func(ALUop));
  ALU_Slice alu_slice_14 (
    .a(InputData1[2]), .b(InputData2[2]), .Q(OutputData[2]), .Cin(alu_slice_15_cout),
    .Cout(alu_slice_14_cout), .Func(ALUop));
  ALU_Slice alu_slice_15 (
    .a(InputData1[1]), .b(InputData2[1]), .Q(OutputData[1]), .Cin(alu_slice_16_cout),
    .Cout(alu_slice_15_cout), .Func(ALUop));
  ALU_Slice alu_slice_16 (
    .a(InputData1[0]), .b(InputData2[0]), .Q(OutputData[0]), .Cin(ALUop[0]), .Cout(alu_slice_16_cout),
    .Func(ALUop));

  assign OutputData[15] = NEGATIVE;
endmodule

module CORE (
  input  CLK,
  input  GLOBAL_RESET,
  input  [15:0] DMro,
  input  [6:0] CHARIN,
  input  VALCHAR,
  input  [15:0] INSTRUCTION,
  output [15:0] PC,
  output [15:0] DMWA,
  output [15:0] DMwd,
  output DMwe,
  output [6:0] CHAROUT,
  output INPUTC,
  output OUTPUTC
);

  wire and_1_out, BLT, BR, control_1_aluinb, control_1_rdst, control_1_rwd, control_1_rwe, control_1_shifte,
       control_1_shiftl, J, JAL, JR, multiplexer_10_out, REG_ALU_negative, REG_ALU_zero;
  wire [1:0] control_1_aluop;
  wire [2:0] control_1_rd, control_1_rs, control_1_rt, control_1_shamt, multiplexer_4_out, multiplexer_6_out,
       multiplexer_7_out;
  wire [5:0] control_1_i_imm;
  wire [7:7] not_1_out;
  wire [11:0] J_Imm;
  wire [15:0] BR_ALU_outputdata, BRImm, CHARIN_t, multiplexer_1_out, multiplexer_2_out, multiplexer_3_out,
       multiplexer_5_out, multiplexer_8_out, multiplexer_9_out, multiplexer_11_out, multiplexer_12_out,
       multiplexer_13_out, PC_1, ShiftLeft_output, ShiftRight_output;
  wire [15:7] CHAROUT_t;

  Multiplexer #(.width(16), .enable("false")) multiplexer_1 (
    .in0(multiplexer_12_out), .in1({CHAROUT_t, CHAROUT}), .out(multiplexer_1_out), .sel(JR));
  // Probe on multiplexer_12_out
  // Probe on PC
  _16_bit_Reg u_PC (.\input (multiplexer_1_out), .RESET(GLOBAL_RESET), .WE(1'b1), .CLK(CLK), .\output (PC));
  not not_1 (not_1_out[7], VALCHAR);
  ALU alu_1 (.ALUop(2'b00), .OutputData(PC_1), .InputData2(16'h1), .InputData1(PC));  // open: OVERFLOW, Zero, NEGATIVE
  _8to16bitZeroExtender u_8to16bitzeroextender_1 (.\input ({not_1_out[7], CHARIN}), .\output (CHARIN_t));
  Multiplexer #(.width(16), .enable("false")) multiplexer_2 (
    .in0(multiplexer_5_out), .in1(PC_1), .out(multiplexer_2_out), .sel(JAL));
  Multiplexer #(.width(16), .enable("false")) multiplexer_3 (
    .in0(multiplexer_2_out), .in1(CHARIN_t), .out(multiplexer_3_out), .sel(INPUTC));
  CONTROL control_1 (
    .Ins_Input(INSTRUCTION), .Rwe(control_1_rwe), .Rdst(control_1_rdst), .ALUinB(control_1_aluinb),
    .ALUop(control_1_aluop), .DMwe(DMwe), .RWD(control_1_rwd), .ShiftE(control_1_shifte), .J_Imm(J_Imm),
    .ShiftL(control_1_shiftl), .BR(BR), .BLT(BLT), .J(J), .Rs(control_1_rs), .JR(JR), .Rt(control_1_rt),
    .JAL(JAL), .INPUTC(INPUTC), .Rd(control_1_rd), .Shamt(control_1_shamt), .OUTPUTC(OUTPUTC),
    .I_Imm(control_1_i_imm));
  Multiplexer #(.width(3), .enable("false")) multiplexer_4 (
    .in0(control_1_rd), .in1(3'b111), .out(multiplexer_4_out), .sel(JAL));
  Multiplexer #(.width(16), .enable("false")) multiplexer_5 (
    .in0(multiplexer_13_out), .in1(multiplexer_8_out), .out(multiplexer_5_out), .sel(control_1_shifte));
  RegFile regfile_1 (
    .CLK(CLK), .GLOBAL_RESET(GLOBAL_RESET), .RS2VAL(DMwd), .RS1VAL({CHAROUT_t, CHAROUT}),
    .GLOBAL_REG_WE(control_1_rwe), .RD(multiplexer_7_out), .RDVAL(multiplexer_3_out), .RS2(control_1_rt),
    .RS1(multiplexer_6_out));
  Multiplexer #(.width(3), .enable("false")) multiplexer_6 (
    .in0(control_1_rs), .in1(multiplexer_7_out), .out(multiplexer_6_out), .sel(JR));
  Multiplexer #(.width(3), .enable("false")) multiplexer_7 (
    .in0(control_1_rt), .in1(multiplexer_4_out), .out(multiplexer_7_out), .sel(control_1_rdst));
  Multiplexer #(.width(16), .enable("false")) multiplexer_8 (
    .in0(ShiftRight_output), .in1(ShiftLeft_output), .out(multiplexer_8_out), .sel(control_1_shiftl));
  ALU BR_ALU (
    .ALUop(2'b00), .OutputData(BR_ALU_outputdata), .InputData2(PC_1), .InputData1(BRImm));  // open: OVERFLOW, Zero, NEGATIVE
  _3_bit_SLL ShiftLeft (.Input({CHAROUT_t, CHAROUT}), .LeftShift(control_1_shamt), .Output(ShiftLeft_output));
  Multiplexer #(.width(16), .enable("false")) multiplexer_9 (
    .in0(DMwd), .in1(BRImm), .out(multiplexer_9_out), .sel(control_1_aluinb));
  _6to16bitSignExtender u_6to16bitsignextender_1 (.\input (control_1_i_imm), .\output (BRImm));
  _3_bit_rsa ShiftRight (.Input({CHAROUT_t, CHAROUT}), .RightShift(control_1_shamt), .Output(ShiftRight_output));
  ALU REG_ALU (
    .ALUop(control_1_aluop), .Zero(REG_ALU_zero), .OutputData(DMWA), .InputData2({CHAROUT_t, CHAROUT}),
    .InputData1(multiplexer_9_out), .NEGATIVE(REG_ALU_negative));  // open: OVERFLOW
  Multiplexer #(.enable("false")) multiplexer_10 (
    .in0(REG_ALU_zero), .in1(REG_ALU_negative), .out(multiplexer_10_out), .sel(BLT));
  Multiplexer #(.width(16), .enable("false")) multiplexer_11 (
    .in0(PC_1), .in1(BR_ALU_outputdata), .out(multiplexer_11_out), .sel(and_1_out));
  and and_1 (and_1_out, multiplexer_10_out, BR);
  // Probe on {PC[15:12], J_Imm}
  Multiplexer #(.width(16), .enable("false")) multiplexer_12 (
    .in0(multiplexer_11_out), .in1({PC[15:12], J_Imm}), .out(multiplexer_12_out), .sel(J));
  Multiplexer #(.width(16), .enable("false")) multiplexer_13 (
    .in0(DMWA), .in1(DMro), .out(multiplexer_13_out), .sel(control_1_rwd));

  // Other names for the same wires on the sheet: JTop4[3:0] = PC[15:12]; CHAROUT_t[6:0] = CHAROUT;
  //   jrrd[15:0] = {CHAROUT_t, CHAROUT}

  // Notes on the sheet:
  //   FETCH
  //   I/O
  //   PC+1
  //   DECODE
  //   EXECUTE
  //   PC CONTROL
  //   BR ARITHMETIC
  //   BRANCH/JUMP LOGIC
  //   MEMORY
  //   READ/WRITE
endmodule

module _3_bit_SLL (
  input  [15:0] Input,
  input  [2:0] LeftShift,
  output [15:0] Output
);

  wire multiplexer_1_out, multiplexer_2_out, multiplexer_3_out, multiplexer_4_out, multiplexer_5_out,
       multiplexer_6_out, multiplexer_7_out, multiplexer_8_out, multiplexer_9_out, multiplexer_10_out,
       multiplexer_11_out, multiplexer_12_out, multiplexer_13_out, multiplexer_14_out, multiplexer_15_out,
       multiplexer_16_out, multiplexer_18_out, multiplexer_19_out, multiplexer_21_out, multiplexer_22_out,
       multiplexer_23_out, multiplexer_26_out, multiplexer_27_out, multiplexer_28_out, multiplexer_29_out,
       multiplexer_31_out, multiplexer_32_out, multiplexer_33_out, multiplexer_35_out, multiplexer_36_out,
       multiplexer_38_out, multiplexer_41_out;

  Multiplexer #(.enable("false")) multiplexer_1 (
    .in0(Input[15]), .in1(Input[14]), .out(multiplexer_1_out), .sel(LeftShift[0]));
  Multiplexer #(.enable("false")) multiplexer_2 (
    .in0(Input[14]), .in1(Input[13]), .out(multiplexer_2_out), .sel(LeftShift[0]));
  Multiplexer #(.enable("false")) multiplexer_3 (
    .in0(Input[13]), .in1(Input[12]), .out(multiplexer_3_out), .sel(LeftShift[0]));
  Multiplexer #(.enable("false")) multiplexer_4 (
    .in0(Input[12]), .in1(Input[11]), .out(multiplexer_4_out), .sel(LeftShift[0]));
  Multiplexer #(.enable("false")) multiplexer_5 (
    .in0(Input[11]), .in1(Input[10]), .out(multiplexer_5_out), .sel(LeftShift[0]));
  Multiplexer #(.enable("false")) multiplexer_6 (
    .in0(multiplexer_1_out), .in1(multiplexer_3_out), .out(multiplexer_6_out), .sel(LeftShift[1]));
  Multiplexer #(.enable("false")) multiplexer_7 (
    .in0(multiplexer_2_out), .in1(multiplexer_4_out), .out(multiplexer_7_out), .sel(LeftShift[1]));
  Multiplexer #(.enable("false")) multiplexer_8 (
    .in0(Input[10]), .in1(Input[9]), .out(multiplexer_8_out), .sel(LeftShift[0]));
  Multiplexer #(.enable("false")) multiplexer_9 (
    .in0(multiplexer_3_out), .in1(multiplexer_5_out), .out(multiplexer_9_out), .sel(LeftShift[1]));
  Multiplexer #(.enable("false")) multiplexer_10 (
    .in0(multiplexer_4_out), .in1(multiplexer_8_out), .out(multiplexer_10_out), .sel(LeftShift[1]));
  Multiplexer #(.enable("false")) multiplexer_11 (
    .in0(Input[9]), .in1(Input[8]), .out(multiplexer_11_out), .sel(LeftShift[0]));
  Multiplexer #(.enable("false")) multiplexer_12 (
    .in0(Input[8]), .in1(Input[7]), .out(multiplexer_12_out), .sel(LeftShift[0]));
  Multiplexer #(.enable("false")) multiplexer_13 (
    .in0(multiplexer_5_out), .in1(multiplexer_11_out), .out(multiplexer_13_out), .sel(LeftShift[1]));
  Multiplexer #(.enable("false")) multiplexer_14 (
    .in0(multiplexer_8_out), .in1(multiplexer_12_out), .out(multiplexer_14_out), .sel(LeftShift[1]));
  Multiplexer #(.enable("false")) multiplexer_15 (
    .in0(Input[7]), .in1(Input[6]), .out(multiplexer_15_out), .sel(LeftShift[0]));
  Multiplexer #(.enable("false")) multiplexer_16 (
    .in0(Input[6]), .in1(Input[5]), .out(multiplexer_16_out), .sel(LeftShift[0]));
  Multiplexer #(.enable("false")) multiplexer_17 (
    .in0(multiplexer_6_out), .in1(multiplexer_13_out), .out(Output[15]), .sel(LeftShift[2]));
  Multiplexer #(.enable("false")) multiplexer_18 (
    .in0(multiplexer_11_out), .in1(multiplexer_15_out), .out(multiplexer_18_out), .sel(LeftShift[1]));
  Multiplexer #(.enable("false")) multiplexer_19 (
    .in0(Input[5]), .in1(Input[4]), .out(multiplexer_19_out), .sel(LeftShift[0]));
  Multiplexer #(.enable("false")) multiplexer_20 (
    .in0(multiplexer_7_out), .in1(multiplexer_14_out), .out(Output[14]), .sel(LeftShift[2]));
  Multiplexer #(.enable("false")) multiplexer_21 (
    .in0(multiplexer_12_out), .in1(multiplexer_16_out), .out(multiplexer_21_out), .sel(LeftShift[1]));
  Multiplexer #(.enable("false")) multiplexer_22 (
    .in0(multiplexer_15_out), .in1(multiplexer_19_out), .out(multiplexer_22_out), .sel(LeftShift[1]));
  Multiplexer #(.enable("false")) multiplexer_23 (
    .in0(Input[4]), .in1(Input[3]), .out(multiplexer_23_out), .sel(LeftShift[0]));
  Multiplexer #(.enable("false")) multiplexer_24 (
    .in0(multiplexer_9_out), .in1(multiplexer_18_out), .out(Output[13]), .sel(LeftShift[2]));
  Multiplexer #(.enable("false")) multiplexer_25 (
    .in0(multiplexer_10_out), .in1(multiplexer_21_out), .out(Output[12]), .sel(LeftShift[2]));
  Multiplexer #(.enable("false")) multiplexer_26 (
    .in0(multiplexer_16_out), .in1(multiplexer_23_out), .out(multiplexer_26_out), .sel(LeftShift[1]));
  Multiplexer #(.enable("false")) multiplexer_27 (
    .in0(multiplexer_19_out), .in1(multiplexer_28_out), .out(multiplexer_27_out), .sel(LeftShift[1]));
  Multiplexer #(.enable("false")) multiplexer_28 (
    .in0(Input[3]), .in1(Input[2]), .out(multiplexer_28_out), .sel(LeftShift[0]));
  Multiplexer #(.enable("false")) multiplexer_29 (
    .in0(Input[2]), .in1(Input[1]), .out(multiplexer_29_out), .sel(LeftShift[0]));
  Multiplexer #(.enable("false")) multiplexer_30 (
    .in0(multiplexer_13_out), .in1(multiplexer_22_out), .out(Output[11]), .sel(LeftShift[2]));
  Multiplexer #(.enable("false")) multiplexer_31 (
    .in0(multiplexer_23_out), .in1(multiplexer_29_out), .out(multiplexer_31_out), .sel(LeftShift[1]));
  Multiplexer #(.enable("false")) multiplexer_32 (
    .in0(multiplexer_28_out), .in1(multiplexer_33_out), .out(multiplexer_32_out), .sel(LeftShift[1]));
  Multiplexer #(.enable("false")) multiplexer_33 (
    .in0(Input[1]), .in1(Input[0]), .out(multiplexer_33_out), .sel(LeftShift[0]));
  Multiplexer #(.enable("false")) multiplexer_34 (
    .in0(multiplexer_14_out), .in1(multiplexer_26_out), .out(Output[10]), .sel(LeftShift[2]));
  Multiplexer #(.enable("false")) multiplexer_35 (
    .in0(multiplexer_29_out), .in1(multiplexer_36_out), .out(multiplexer_35_out), .sel(LeftShift[1]));
  Multiplexer #(.enable("false")) multiplexer_36 (
    .in0(Input[0]), .in1(1'b0), .out(multiplexer_36_out), .sel(LeftShift[0]));
  Multiplexer #(.enable("false")) multiplexer_37 (
    .in0(multiplexer_18_out), .in1(multiplexer_27_out), .out(Output[9]), .sel(LeftShift[2]));
  Multiplexer #(.enable("false")) multiplexer_38 (
    .in0(multiplexer_33_out), .in1(1'b0), .out(multiplexer_38_out), .sel(LeftShift[1]));
  Multiplexer #(.enable("false")) multiplexer_39 (
    .in0(multiplexer_21_out), .in1(multiplexer_31_out), .out(Output[8]), .sel(LeftShift[2]));
  Multiplexer #(.enable("false")) multiplexer_40 (
    .in0(multiplexer_22_out), .in1(multiplexer_32_out), .out(Output[7]), .sel(LeftShift[2]));
  Multiplexer #(.enable("false")) multiplexer_41 (
    .in0(multiplexer_36_out), .in1(1'b0), .out(multiplexer_41_out), .sel(LeftShift[1]));
  Multiplexer #(.enable("false")) multiplexer_42 (
    .in0(multiplexer_26_out), .in1(multiplexer_35_out), .out(Output[6]), .sel(LeftShift[2]));
  Multiplexer #(.enable("false")) multiplexer_43 (
    .in0(multiplexer_27_out), .in1(multiplexer_38_out), .out(Output[5]), .sel(LeftShift[2]));
  Multiplexer #(.enable("false")) multiplexer_44 (
    .in0(multiplexer_31_out), .in1(multiplexer_41_out), .out(Output[4]), .sel(LeftShift[2]));
  Multiplexer #(.enable("false")) multiplexer_45 (
    .in0(multiplexer_32_out), .in1(1'b0), .out(Output[3]), .sel(LeftShift[2]));
  Multiplexer #(.enable("false")) multiplexer_46 (
    .in0(multiplexer_35_out), .in1(1'b0), .out(Output[2]), .sel(LeftShift[2]));
  Multiplexer #(.enable("false")) multiplexer_47 (
    .in0(multiplexer_38_out), .in1(1'b0), .out(Output[1]), .sel(LeftShift[2]));
  Multiplexer #(.enable("false")) multiplexer_48 (
    .in0(multiplexer_41_out), .in1(1'b0), .out(Output[0]), .sel(LeftShift[2]));

  // Other names for the same wires on the sheet: sel0 = LeftShift[0]; sel1 = LeftShift[1]; sel2 = LeftShift[2]
endmodule

module _3_bit_rsa (
  input  [15:0] Input,
  input  [2:0] RightShift,
  output [15:0] Output
);

  wire multiplexer_1_out, multiplexer_2_out, multiplexer_3_out, multiplexer_4_out, multiplexer_5_out,
       multiplexer_6_out, multiplexer_7_out, multiplexer_8_out, multiplexer_9_out, multiplexer_10_out,
       multiplexer_11_out, multiplexer_12_out, multiplexer_13_out, multiplexer_14_out, multiplexer_15_out,
       multiplexer_16_out, multiplexer_18_out, multiplexer_19_out, multiplexer_21_out, multiplexer_22_out,
       multiplexer_23_out, multiplexer_26_out, multiplexer_27_out, multiplexer_28_out, multiplexer_29_out,
       multiplexer_31_out, multiplexer_32_out, multiplexer_33_out, multiplexer_35_out, multiplexer_37_out,
       multiplexer_40_out;

  Multiplexer #(.enable("false")) multiplexer_1 (
    .in0(Input[0]), .in1(Input[1]), .out(multiplexer_1_out), .sel(RightShift[0]));
  Multiplexer #(.enable("false")) multiplexer_2 (
    .in0(Input[1]), .in1(Input[2]), .out(multiplexer_2_out), .sel(RightShift[0]));
  Multiplexer #(.enable("false")) multiplexer_3 (
    .in0(Input[2]), .in1(Input[3]), .out(multiplexer_3_out), .sel(RightShift[0]));
  Multiplexer #(.enable("false")) multiplexer_4 (
    .in0(Input[3]), .in1(Input[4]), .out(multiplexer_4_out), .sel(RightShift[0]));
  Multiplexer #(.enable("false")) multiplexer_5 (
    .in0(Input[4]), .in1(Input[5]), .out(multiplexer_5_out), .sel(RightShift[0]));
  Multiplexer #(.enable("false")) multiplexer_6 (
    .in0(multiplexer_1_out), .in1(multiplexer_3_out), .out(multiplexer_6_out), .sel(RightShift[1]));
  Multiplexer #(.enable("false")) multiplexer_7 (
    .in0(multiplexer_2_out), .in1(multiplexer_4_out), .out(multiplexer_7_out), .sel(RightShift[1]));
  Multiplexer #(.enable("false")) multiplexer_8 (
    .in0(Input[5]), .in1(Input[6]), .out(multiplexer_8_out), .sel(RightShift[0]));
  Multiplexer #(.enable("false")) multiplexer_9 (
    .in0(multiplexer_3_out), .in1(multiplexer_5_out), .out(multiplexer_9_out), .sel(RightShift[1]));
  Multiplexer #(.enable("false")) multiplexer_10 (
    .in0(multiplexer_4_out), .in1(multiplexer_8_out), .out(multiplexer_10_out), .sel(RightShift[1]));
  Multiplexer #(.enable("false")) multiplexer_11 (
    .in0(Input[6]), .in1(Input[7]), .out(multiplexer_11_out), .sel(RightShift[0]));
  Multiplexer #(.enable("false")) multiplexer_12 (
    .in0(Input[7]), .in1(Input[8]), .out(multiplexer_12_out), .sel(RightShift[0]));
  Multiplexer #(.enable("false")) multiplexer_13 (
    .in0(multiplexer_5_out), .in1(multiplexer_11_out), .out(multiplexer_13_out), .sel(RightShift[1]));
  Multiplexer #(.enable("false")) multiplexer_14 (
    .in0(multiplexer_8_out), .in1(multiplexer_12_out), .out(multiplexer_14_out), .sel(RightShift[1]));
  Multiplexer #(.enable("false")) multiplexer_15 (
    .in0(Input[8]), .in1(Input[9]), .out(multiplexer_15_out), .sel(RightShift[0]));
  Multiplexer #(.enable("false")) multiplexer_16 (
    .in0(Input[9]), .in1(Input[10]), .out(multiplexer_16_out), .sel(RightShift[0]));
  Multiplexer #(.enable("false")) multiplexer_17 (
    .in0(multiplexer_6_out), .in1(multiplexer_13_out), .out(Output[0]), .sel(RightShift[2]));
  Multiplexer #(.enable("false")) multiplexer_18 (
    .in0(multiplexer_11_out), .in1(multiplexer_15_out), .out(multiplexer_18_out), .sel(RightShift[1]));
  Multiplexer #(.enable("false")) multiplexer_19 (
    .in0(Input[10]), .in1(Input[11]), .out(multiplexer_19_out), .sel(RightShift[0]));
  Multiplexer #(.enable("false")) multiplexer_20 (
    .in0(multiplexer_7_out), .in1(multiplexer_14_out), .out(Output[1]), .sel(RightShift[2]));
  Multiplexer #(.enable("false")) multiplexer_21 (
    .in0(multiplexer_12_out), .in1(multiplexer_16_out), .out(multiplexer_21_out), .sel(RightShift[1]));
  Multiplexer #(.enable("false")) multiplexer_22 (
    .in0(multiplexer_15_out), .in1(multiplexer_19_out), .out(multiplexer_22_out), .sel(RightShift[1]));
  Multiplexer #(.enable("false")) multiplexer_23 (
    .in0(Input[11]), .in1(Input[12]), .out(multiplexer_23_out), .sel(RightShift[0]));
  Multiplexer #(.enable("false")) multiplexer_24 (
    .in0(multiplexer_9_out), .in1(multiplexer_18_out), .out(Output[2]), .sel(RightShift[2]));
  Multiplexer #(.enable("false")) multiplexer_25 (
    .in0(multiplexer_10_out), .in1(multiplexer_21_out), .out(Output[3]), .sel(RightShift[2]));
  Multiplexer #(.enable("false")) multiplexer_26 (
    .in0(multiplexer_16_out), .in1(multiplexer_23_out), .out(multiplexer_26_out), .sel(RightShift[1]));
  Multiplexer #(.enable("false")) multiplexer_27 (
    .in0(multiplexer_19_out), .in1(multiplexer_28_out), .out(multiplexer_27_out), .sel(RightShift[1]));
  Multiplexer #(.enable("false")) multiplexer_28 (
    .in0(Input[12]), .in1(Input[13]), .out(multiplexer_28_out), .sel(RightShift[0]));
  Multiplexer #(.enable("false")) multiplexer_29 (
    .in0(Input[13]), .in1(Input[14]), .out(multiplexer_29_out), .sel(RightShift[0]));
  Multiplexer #(.enable("false")) multiplexer_30 (
    .in0(multiplexer_13_out), .in1(multiplexer_22_out), .out(Output[4]), .sel(RightShift[2]));
  Multiplexer #(.enable("false")) multiplexer_31 (
    .in0(multiplexer_23_out), .in1(multiplexer_29_out), .out(multiplexer_31_out), .sel(RightShift[1]));
  Multiplexer #(.enable("false")) multiplexer_32 (
    .in0(multiplexer_28_out), .in1(multiplexer_33_out), .out(multiplexer_32_out), .sel(RightShift[1]));
  Multiplexer #(.enable("false")) multiplexer_33 (
    .in0(Input[14]), .in1(Input[15]), .out(multiplexer_33_out), .sel(RightShift[0]));
  Multiplexer #(.enable("false")) multiplexer_34 (
    .in0(multiplexer_14_out), .in1(multiplexer_26_out), .out(Output[5]), .sel(RightShift[2]));
  Multiplexer #(.enable("false")) multiplexer_35 (
    .in0(multiplexer_29_out), .in1(Input[15]), .out(multiplexer_35_out), .sel(RightShift[1]));
  Multiplexer #(.enable("false")) multiplexer_36 (
    .in0(multiplexer_18_out), .in1(multiplexer_27_out), .out(Output[6]), .sel(RightShift[2]));
  Multiplexer #(.enable("false")) multiplexer_37 (
    .in0(multiplexer_33_out), .in1(Input[15]), .out(multiplexer_37_out), .sel(RightShift[1]));
  Multiplexer #(.enable("false")) multiplexer_38 (
    .in0(multiplexer_21_out), .in1(multiplexer_31_out), .out(Output[7]), .sel(RightShift[2]));
  Multiplexer #(.enable("false")) multiplexer_39 (
    .in0(multiplexer_22_out), .in1(multiplexer_32_out), .out(Output[8]), .sel(RightShift[2]));
  Multiplexer #(.enable("false")) multiplexer_40 (
    .in0(Input[15]), .in1(Input[15]), .out(multiplexer_40_out), .sel(RightShift[1]));
  Multiplexer #(.enable("false")) multiplexer_41 (
    .in0(multiplexer_26_out), .in1(multiplexer_35_out), .out(Output[9]), .sel(RightShift[2]));
  Multiplexer #(.enable("false")) multiplexer_42 (
    .in0(multiplexer_27_out), .in1(multiplexer_37_out), .out(Output[10]), .sel(RightShift[2]));
  Multiplexer #(.enable("false")) multiplexer_43 (
    .in0(multiplexer_31_out), .in1(multiplexer_40_out), .out(Output[11]), .sel(RightShift[2]));
  Multiplexer #(.enable("false")) multiplexer_44 (
    .in0(multiplexer_32_out), .in1(Input[15]), .out(Output[12]), .sel(RightShift[2]));
  Multiplexer #(.enable("false")) multiplexer_45 (
    .in0(multiplexer_35_out), .in1(Input[15]), .out(Output[13]), .sel(RightShift[2]));
  Multiplexer #(.enable("false")) multiplexer_46 (
    .in0(multiplexer_37_out), .in1(Input[15]), .out(Output[14]), .sel(RightShift[2]));
  Multiplexer #(.enable("false")) multiplexer_47 (
    .in0(multiplexer_40_out), .in1(Input[15]), .out(Output[15]), .sel(RightShift[2]));

  // Other names for the same wires on the sheet: sel0 = RightShift[0]; sel1 = RightShift[1]; sel2 = RightShift[2]
endmodule

module Opcode_Decoder (
  input  [3:0] OPCODE,
  output [1:0] ALUop,
  output Rwe,
  output Rdst,
  output ALUinB,
  output DMwe,
  output RWD,
  output ShiftE,
  output ShiftL,
  output BR,
  output BLT,
  output J,
  output JR,
  output JAL,
  output INPUTC,
  output OUTPUTC
);

  wire decoder_1_out0, decoder_1_out1, decoder_1_out2, decoder_1_out3, decoder_1_out4, decoder_1_out6,
       decoder_1_out9, decoder_1_out11;

  Decoder #(.select(4), .enable("false")) decoder_1 (
    .out0(decoder_1_out0), .out1(decoder_1_out1), .out2(decoder_1_out2), .out3(decoder_1_out3),
    .out4(decoder_1_out4), .out5(ShiftL), .out6(decoder_1_out6), .out7(RWD), .out8(DMwe),
    .out9(decoder_1_out9), .out10(BLT), .out11(decoder_1_out11), .out12(JR), .out13(JAL), .out14(INPUTC),
    .out15(OUTPUTC), .sel(OPCODE));
  or or_1 (Rwe, decoder_1_out0, decoder_1_out1, decoder_1_out2, decoder_1_out3, decoder_1_out4, ShiftL, decoder_1_out6, RWD, JAL, INPUTC);
  or or_2 (Rdst, decoder_1_out0, decoder_1_out2, decoder_1_out3, decoder_1_out4, JR, ShiftL, decoder_1_out6, JAL, INPUTC);
  or or_3 (ALUinB, decoder_1_out1, RWD, DMwe);
  or or_4 (ALUop[1], decoder_1_out3, decoder_1_out4);
  or or_5 (ALUop[0], decoder_1_out2, decoder_1_out4, decoder_1_out9, BLT);
  or or_6 (ShiftE, ShiftL, decoder_1_out6);
  or or_7 (BR, decoder_1_out9, BLT);
  or or_8 (J, decoder_1_out11, JAL);
endmodule

module CONTROL (
  input  [15:0] Ins_Input,
  output Rwe,
  output Rdst,
  output ALUinB,
  output [1:0] ALUop,
  output DMwe,
  output RWD,
  output ShiftE,
  output ShiftL,
  output BR,
  output BLT,
  output J,
  output JR,
  output JAL,
  output INPUTC,
  output OUTPUTC,
  output [11:0] J_Imm,
  output [2:0] Rs,
  output [2:0] Rt,
  output [2:0] Rd,
  output [2:0] Shamt,
  output [5:0] I_Imm
);

  Opcode_Decoder opcode_decoder_1 (
    .Rwe(Rwe), .Rdst(Rdst), .ALUinB(ALUinB), .ALUop(ALUop), .DMwe(DMwe), .RWD(RWD), .ShiftE(ShiftE),
    .ShiftL(ShiftL), .BR(BR), .BLT(BLT), .J(J), .JR(JR), .JAL(JAL), .INPUTC(INPUTC), .OUTPUTC(OUTPUTC),
    .OPCODE(Ins_Input[15:12]));

  assign I_Imm = Ins_Input[5:0];
  assign J_Imm = Ins_Input[11:0];
  assign Rd = Ins_Input[5:3];
  assign Rs = Ins_Input[11:9];
  assign Rt = Ins_Input[8:6];
  assign Shamt = Ins_Input[2:0];
endmodule

module _8to16bitZeroExtender (
  input  [7:0] \input ,
  output [15:0] \output 
);


  assign \output  = {{8{1'b0}}, \input };
endmodule

module _6to16bitSignExtender (
  input  [5:0] \input ,
  output [15:0] \output 
);


  assign \output  = {{11{\input [5]}}, \input [4:0]};
endmodule
